# Fritzing sketch dancing_leds (saved by Fritzing 1.0.4)
breadboards: 1

parts:
  Particle_Photon_2 = photon2
  Kitronik_Linear_Actuator_Kit = Basic Servo
  Adafruit_PDM_MEMS_Microphone_Breakout = Adafruit PDM Mic [part_number="Adafruit #3492"]
  Adafruit_NeoPixel_Ring_12 = 12 NeoPixel Ring [part_number=1643]

nets:
  N1: Particle_Photon_2.Pin_2, Particle_Photon_2.Pin_31, Adafruit_PDM_MEMS_Microphone_Breakout.VDD
  N2: Particle_Photon_2.Pin_4, Particle_Photon_2.Pin_30, Adafruit_PDM_MEMS_Microphone_Breakout.GND
  N3: Particle_Photon_2.Pin_5, Adafruit_PDM_MEMS_Microphone_Breakout.CLK
  N4: Particle_Photon_2.Pin_6, Adafruit_PDM_MEMS_Microphone_Breakout.DATA
  N5: Particle_Photon_2.Pin_18, Kitronik_Linear_Actuator_Kit.pulse
  N6: Particle_Photon_2.Pin_19, Adafruit_NeoPixel_Ring_12.IN
  VCC: Particle_Photon_2.Pin_26, Kitronik_Linear_Actuator_Kit.vcc, Adafruit_NeoPixel_Ring_12.VDD
  N7: Particle_Photon_2.Pin_28, Particle_Photon_2.Pin_29
  GND: Kitronik_Linear_Actuator_Kit.gnd, Adafruit_NeoPixel_Ring_12.GND

custom parts:
  photon2: The Photon 2 is a development module with a microcontroller and Wi-Fi networking.
  Adafruit PDM Mic: An exotic new microphone has arrived in the Adafruit shop, a PDM MEMS Microphone! PDM is the 'third' kind of microphone you can integrate with electronics, apart from analog or I2S. These microphones are very commonly used in products, but are rarely seen in maker projects. Still, they have some benefits so we thought we'd offer a breakout for the shop. The first thing to note is that this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
  12 NeoPixel Ring: 12 ultra bright smart LED NeoPixels are arranged in a circle with 1.5" (37mm) outer diameter. The rings are 'chainable' - connect the output pin of one to the input pin of another. Use only one microcontroller pin to control as many as you can chain together! Each LED is addressable as the driver chip is inside the LED. Each one has ~18mA constant current drive so the color will be very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
